// Logisim project J.circ as structural Verilog: 11 circuits, main circuit main
module main (
);

  wire bianmaqi16to4_1_out_17, bianmaqi16to4_1_out_18, bianmaqi16to4_1_out_19, bianmaqi16to4_1_out_20,
       dipswitch_1_p1, dipswitch_1_p2, dipswitch_1_p3, dipswitch_1_p4, dipswitch_1_p5, dipswitch_1_p6,
       dipswitch_1_p7, dipswitch_1_p8, dipswitch_1_p9, dipswitch_1_p10, dipswitch_1_p11, dipswitch_1_p12,
       dipswitch_1_p13, dipswitch_1_p14, dipswitch_1_p15, dipswitch_1_p16, shumaguanyimaqi16_1_a,
       shumaguanyimaqi16_1_b, shumaguanyimaqi16_1_c, shumaguanyimaqi16_1_d, shumaguanyimaqi16_1_e,
       shumaguanyimaqi16_1_f, shumaguanyimaqi16_1_g;

  // DipSwitch #(.number(16)) dipswitch_1: pin names not known; wires that end beside it: dipswitch_1_p1, dipswitch_1_p2, dipswitch_1_p3, dipswitch_1_p4, dipswitch_1_p5, dipswitch_1_p6, dipswitch_1_p7, dipswitch_1_p8, dipswitch_1_p9, dipswitch_1_p10, dipswitch_1_p11, dipswitch_1_p12, dipswitch_1_p13, dipswitch_1_p14, dipswitch_1_p15, dipswitch_1_p16
  bianmaqi16to4 bianmaqi16to4_1 (
    .i1(dipswitch_1_p1), .i2(dipswitch_1_p2), .i3(dipswitch_1_p3), .i4(dipswitch_1_p4), .i5(dipswitch_1_p5),
    .i6(dipswitch_1_p6), .i7(dipswitch_1_p7), .i8(dipswitch_1_p8), .i9(dipswitch_1_p9),
    .i10(dipswitch_1_p10), .i11(dipswitch_1_p11), .i12(dipswitch_1_p12), .i13(dipswitch_1_p13),
    .i14(dipswitch_1_p14), .i15(dipswitch_1_p15), .i16(dipswitch_1_p16), .out_17(bianmaqi16to4_1_out_17),
    .out_18(bianmaqi16to4_1_out_18), .out_19(bianmaqi16to4_1_out_19), .out_20(bianmaqi16to4_1_out_20));
  shumaguanyimaqi16 shumaguanyimaqi16_1 (
    .in_1(bianmaqi16to4_1_out_17), .in_2(bianmaqi16to4_1_out_18), .in_3(bianmaqi16to4_1_out_19),
    .in_4(bianmaqi16to4_1_out_20), .a(shumaguanyimaqi16_1_a), .b(shumaguanyimaqi16_1_b),
    .c(shumaguanyimaqi16_1_c), .d(shumaguanyimaqi16_1_d), .e(shumaguanyimaqi16_1_e),
    .f(shumaguanyimaqi16_1_f), .g(shumaguanyimaqi16_1_g));
  _7_Segment_Display u_7_segment_display_1 (
    .g(shumaguanyimaqi16_1_g), .f(shumaguanyimaqi16_1_f), .a(shumaguanyimaqi16_1_a),
    .b(shumaguanyimaqi16_1_b), .e(shumaguanyimaqi16_1_e), .d(shumaguanyimaqi16_1_d), .c(shumaguanyimaqi16_1_c));  // open: dp
endmodule

module tonghuo_men (
  input  in_1,
  input  in_2,
  output out_3
);

  wire nand_1_out, or_1_out;

  or or_1 (or_1_out, in_1, in_2);
  nand nand_1 (nand_1_out, in_1, in_2);
  nand nand_2 (out_3, or_1_out, nand_1_out);
endmodule

module yihuo_men (
  input  in_1,
  input  in_2,
  output out_3
);

  wire and_1_out, nor_1_out;

  and and_1 (and_1_out, in_1, in_2);
  nor nor_1 (nor_1_out, in_1, in_2);
  nor nor_2 (out_3, and_1_out, nor_1_out);
endmodule

module huomen (
  input  in_1,
  input  in_2,
  output out_3
);

  wire transistor_1_out, transistor_2_out;

  Transistor transistor_1 (.in(1'b1), .out(transistor_1_out), .gate(in_1));
  Transistor transistor_2 (.in(transistor_1_out), .out(transistor_2_out), .gate(in_2));
  Transistor #(.\type ("n")) transistor_3 (.in(1'b0), .out(transistor_2_out), .gate(in_1));
  Transistor #(.\type ("n")) transistor_4 (.in(1'b0), .out(transistor_2_out), .gate(in_2));
  Transistor transistor_5 (.in(1'b1), .out(out_3), .gate(transistor_2_out));
  Transistor #(.\type ("n")) transistor_6 (.in(1'b0), .out(out_3), .gate(transistor_2_out));
endmodule

module tonghuo_quan (
  input  in_1,
  input  in_2,
  output out_3
);

  wire transistor_1_out;

  Transistor transistor_1 (.in(1'b1), .out(transistor_1_out), .gate(in_2));
  Transistor #(.\type ("n")) transistor_2 (.in(1'b0), .out(transistor_1_out), .gate(in_2));
  Transistor transistor_3 (.in(transistor_1_out), .out(out_3), .gate(in_1));
  Transistor #(.\type ("n")) transistor_4 (.in(in_2), .out(out_3), .gate(in_1));
  // Transmission_Gate transmission_1: pin names not known; wires that end beside it: out_3, transistor_1_out, in_2, in_1
endmodule

module yihuo_quan (
  input  in_1,
  input  in_2,
  output out_3
);

  wire transistor_3_out;

  Transistor transistor_1 (.in(in_2), .out(out_3), .gate(in_1));
  Transistor #(.\type ("n")) transistor_2 (.in(transistor_3_out), .out(out_3), .gate(in_1));
  Transistor transistor_3 (.in(1'b1), .out(transistor_3_out), .gate(in_2));
  Transistor #(.\type ("n")) transistor_4 (.in(1'b0), .out(transistor_3_out), .gate(in_2));
  // Transmission_Gate transmission_1: pin names not known; wires that end beside it: out_3, in_2, transistor_3_out, in_1
endmodule

module yimaqi2to4 (
  input  in_1,
  input  in_2,
  input  in_3,
  output out_4,
  output out_5,
  output out_6,
  output out_7
);

  and and_1 (out_4, ~in_1, in_3, ~in_2);  // AND_Gate
  and and_2 (out_5, in_1, in_3, ~in_2);  // AND_Gate
  and and_3 (out_6, ~in_1, in_3, in_2);  // AND_Gate
  and and_4 (out_7, in_1, in_3, in_2);
endmodule

module yimaqi3to8 (
  input  zero,
  input  one,
  input  two,
  input  en,
  output out_5,
  output out_6,
  output out_7,
  output out_8,
  output out_9,
  output out_10,
  output out_11,
  output out_12
);

  wire and_1_out, and_2_out, not_1_out, yimaqi2to4_1_out_4, yimaqi2to4_2_out_4;

  and and_1 (and_1_out, en, zero);
  and and_2 (and_2_out, one, en);
  not not_1 (not_1_out, two);
  yimaqi2to4 yimaqi2to4_1 (
    .in_1(and_1_out), .in_2(and_2_out), .in_3(not_1_out), .out_4(yimaqi2to4_1_out_4), .out_5(out_6),
    .out_6(out_7), .out_7(out_8));
  yimaqi2to4 yimaqi2to4_2 (
    .in_1(and_1_out), .in_2(and_2_out), .in_3(two), .out_4(yimaqi2to4_2_out_4), .out_5(out_10),
    .out_6(out_11), .out_7(out_12));
  and and_3 (out_9, en, yimaqi2to4_2_out_4);
  and and_4 (out_5, en, yimaqi2to4_1_out_4);
endmodule

module shumaguanyimaqi10 (
  input  zero,
  input  one,
  input  two,
  input  three,
  output a,
  output b,
  output c,
  output d,
  output e,
  output f,
  output g
);

  wire and_1_out, and_2_out, yimaqi3to8_1_out_5, yimaqi3to8_1_out_6, yimaqi3to8_1_out_7, yimaqi3to8_1_out_8,
       yimaqi3to8_1_out_9, yimaqi3to8_1_out_10, yimaqi3to8_1_out_11, yimaqi3to8_1_out_12;

  yimaqi3to8 yimaqi3to8_1 (
    .zero(zero), .one(one), .two(two), .en(1'b1), .out_5(yimaqi3to8_1_out_5), .out_6(yimaqi3to8_1_out_6),
    .out_7(yimaqi3to8_1_out_7), .out_8(yimaqi3to8_1_out_8), .out_9(yimaqi3to8_1_out_9),
    .out_10(yimaqi3to8_1_out_10), .out_11(yimaqi3to8_1_out_11), .out_12(yimaqi3to8_1_out_12));
  and and_1 (and_1_out, ~zero, three);  // AND_Gate
  and and_2 (and_2_out, zero, three);
  or or_1 (a, yimaqi3to8_1_out_5, yimaqi3to8_1_out_7, yimaqi3to8_1_out_8, yimaqi3to8_1_out_10, yimaqi3to8_1_out_11, yimaqi3to8_1_out_12, and_1_out, and_2_out);
  or or_2 (b, yimaqi3to8_1_out_5, yimaqi3to8_1_out_6, yimaqi3to8_1_out_7, yimaqi3to8_1_out_8, yimaqi3to8_1_out_9, yimaqi3to8_1_out_12, and_1_out, and_2_out);
  or or_3 (c, yimaqi3to8_1_out_5, yimaqi3to8_1_out_6, yimaqi3to8_1_out_8, yimaqi3to8_1_out_9, yimaqi3to8_1_out_10, yimaqi3to8_1_out_11, yimaqi3to8_1_out_12, and_1_out, and_2_out);
  or or_4 (d, yimaqi3to8_1_out_5, yimaqi3to8_1_out_7, yimaqi3to8_1_out_8, yimaqi3to8_1_out_10, yimaqi3to8_1_out_11, and_1_out, and_2_out);
  or or_5 (e, yimaqi3to8_1_out_5, yimaqi3to8_1_out_7, yimaqi3to8_1_out_11, and_1_out);
  or or_6 (f, yimaqi3to8_1_out_5, yimaqi3to8_1_out_9, yimaqi3to8_1_out_10, yimaqi3to8_1_out_11, and_1_out, and_2_out);
  or or_7 (g, yimaqi3to8_1_out_7, yimaqi3to8_1_out_8, yimaqi3to8_1_out_9, yimaqi3to8_1_out_10, yimaqi3to8_1_out_11, and_1_out, and_2_out);
endmodule

module shumaguanyimaqi16 (
  input  in_1,
  input  in_2,
  input  in_3,
  input  in_4,
  output a,
  output b,
  output c,
  output d,
  output e,
  output f,
  output g
);

  wire not_1_out, or_1_out, or_2_out, or_3_out, or_4_out, or_5_out, or_6_out, or_7_out, yimaqi3to8_1_out_5,
       yimaqi3to8_1_out_6, yimaqi3to8_1_out_7, yimaqi3to8_1_out_8, yimaqi3to8_1_out_9, yimaqi3to8_1_out_10,
       yimaqi3to8_1_out_11, yimaqi3to8_1_out_12, yimaqi3to8_2_out_5, yimaqi3to8_2_out_6, yimaqi3to8_2_out_7,
       yimaqi3to8_2_out_8, yimaqi3to8_2_out_9, yimaqi3to8_2_out_10, yimaqi3to8_2_out_11, yimaqi3to8_2_out_12;

  not not_1 (not_1_out, in_4);
  yimaqi3to8 yimaqi3to8_1 (
    .zero(in_1), .one(in_2), .two(in_3), .en(not_1_out), .out_5(yimaqi3to8_1_out_5),
    .out_6(yimaqi3to8_1_out_6), .out_7(yimaqi3to8_1_out_7), .out_8(yimaqi3to8_1_out_8),
    .out_9(yimaqi3to8_1_out_9), .out_10(yimaqi3to8_1_out_10), .out_11(yimaqi3to8_1_out_11),
    .out_12(yimaqi3to8_1_out_12));
  yimaqi3to8 yimaqi3to8_2 (
    .zero(in_1), .one(in_2), .two(in_3), .en(in_4), .out_5(yimaqi3to8_2_out_5), .out_6(yimaqi3to8_2_out_6),
    .out_7(yimaqi3to8_2_out_7), .out_8(yimaqi3to8_2_out_8), .out_9(yimaqi3to8_2_out_9),
    .out_10(yimaqi3to8_2_out_10), .out_11(yimaqi3to8_2_out_11), .out_12(yimaqi3to8_2_out_12));
  or or_1 (or_1_out, yimaqi3to8_1_out_5, yimaqi3to8_1_out_7, yimaqi3to8_1_out_8, yimaqi3to8_1_out_10, yimaqi3to8_1_out_11, yimaqi3to8_1_out_12, yimaqi3to8_2_out_5, yimaqi3to8_2_out_6);
  or or_2 (or_2_out, yimaqi3to8_1_out_5, yimaqi3to8_1_out_6, yimaqi3to8_1_out_7, yimaqi3to8_1_out_8, yimaqi3to8_1_out_9, yimaqi3to8_1_out_12, yimaqi3to8_2_out_5, yimaqi3to8_2_out_6);
  or or_3 (or_3_out, yimaqi3to8_1_out_5, yimaqi3to8_1_out_6, yimaqi3to8_1_out_8, yimaqi3to8_1_out_9, yimaqi3to8_1_out_10, yimaqi3to8_1_out_11, yimaqi3to8_1_out_12, yimaqi3to8_2_out_5, yimaqi3to8_2_out_6);
  or or_4 (or_4_out, yimaqi3to8_1_out_5, yimaqi3to8_1_out_7, yimaqi3to8_1_out_8, yimaqi3to8_1_out_10, yimaqi3to8_1_out_11, yimaqi3to8_2_out_5, yimaqi3to8_2_out_6);
  or or_5 (or_5_out, yimaqi3to8_1_out_5, yimaqi3to8_1_out_7, yimaqi3to8_1_out_11, yimaqi3to8_2_out_5);
  or or_6 (or_6_out, yimaqi3to8_1_out_5, yimaqi3to8_1_out_9, yimaqi3to8_1_out_10, yimaqi3to8_1_out_11, yimaqi3to8_2_out_5, yimaqi3to8_2_out_6);
  or or_7 (or_7_out, yimaqi3to8_1_out_7, yimaqi3to8_1_out_8, yimaqi3to8_1_out_9, yimaqi3to8_1_out_10, yimaqi3to8_1_out_11, yimaqi3to8_2_out_5, yimaqi3to8_2_out_6);
  or or_8 (a, or_1_out, yimaqi3to8_2_out_7, yimaqi3to8_2_out_9, yimaqi3to8_2_out_11, yimaqi3to8_2_out_12);
  or or_9 (b, or_2_out, yimaqi3to8_2_out_7, yimaqi3to8_2_out_10);
  or or_10 (c, or_3_out, yimaqi3to8_2_out_7, yimaqi3to8_2_out_8, yimaqi3to8_2_out_10);
  or or_11 (d, or_4_out, yimaqi3to8_2_out_8, yimaqi3to8_2_out_9, yimaqi3to8_2_out_10, yimaqi3to8_2_out_11);
  or or_12 (e, or_5_out, yimaqi3to8_2_out_7, yimaqi3to8_2_out_8, yimaqi3to8_2_out_9, yimaqi3to8_2_out_10, yimaqi3to8_2_out_11, yimaqi3to8_2_out_12);
  or or_13 (f, or_6_out, yimaqi3to8_2_out_7, yimaqi3to8_2_out_8, yimaqi3to8_2_out_9, yimaqi3to8_2_out_11, yimaqi3to8_2_out_12);
  or or_14 (g, or_7_out, yimaqi3to8_2_out_7, yimaqi3to8_2_out_8, yimaqi3to8_2_out_10, yimaqi3to8_2_out_11, yimaqi3to8_2_out_12);
endmodule

module bianmaqi16to4 (
  input  i1,
  input  i2,
  input  i3,
  input  i4,
  input  i5,
  input  i6,
  input  i7,
  input  i8,
  input  i9,
  input  i10,
  input  i11,
  input  i12,
  input  i13,
  input  i14,
  input  i15,
  input  i16,
  output out_17,
  output out_18,
  output out_19,
  output out_20
);

  or or_1 (out_17, i2, i4, i6, i8, i10, i12, i14, i16);
  or or_2 (out_18, i3, i4, i7, i8, i11, i12, i15, i16);
  or or_3 (out_19, i5, i6, i7, i8, i13, i14, i15, i16);
  or or_4 (out_20, i9, i10, i11, i12, i13, i14, i15, i16);
endmodule
